// Logisim project 2.5.a.circ as structural Verilog: 1 circuit, main circuit main
module main (
  input  a,
  input  b,
  input  c,
  output out_4
);

  wire nor_1_out, not_1_out, not_2_out, not_3_out, not_4_out;

  not not_1 (not_1_out, a);
  not not_2 (not_2_out, b);
  not not_3 (not_3_out, c);
  not not_4 (not_4_out, nor_1_out);
  nor nor_1 (nor_1_out, not_1_out, not_2_out);
  nor nor_2 (out_4, not_4_out, not_3_out);

  // Notes on the sheet:
  //   2.5.a
endmodule
