// Logisim project 2.7.circ as structural Verilog: 1 circuit, main circuit main
module main (
  input  c_1,
  input  c_0,
  input  e_0,
  output s_0,
  output s_1,
  output s_2,
  output s_3
);

  wire and_1_out, and_2_out, and_3_out, and_4_out, not_1_out, not_2_out, not_3_out, not_4_out;

  not not_1 (not_1_out, c_1);
  not not_2 (not_2_out, c_0);
  not not_3 (not_3_out, c_1);
  not not_4 (not_4_out, c_0);
  and and_1 (and_1_out, not_1_out, not_2_out);
  and and_2 (and_2_out, not_3_out, c_0);
  and and_3 (and_3_out, c_1, not_4_out);
  and and_4 (and_4_out, c_1, c_0);
  and and_5 (s_0, and_1_out, e_0);
  and and_6 (s_1, and_2_out, e_0);
  and and_7 (s_2, and_3_out, e_0);
  and and_8 (s_3, and_4_out, e_0);
endmodule
