// Logisim project 2.8.a.circ as structural Verilog: 1 circuit, main circuit main
module main (
  input  e3,
  input  e2,
  input  e1,
  input  e0,
  output s0,
  output s1
);

  wire nor_1_out, nor_2_out, xor_1_out, xor_2_out;

  xor xor_1 (xor_1_out, e3, e2);
  nor nor_1 (nor_1_out, e1, e0);
  nor nor_2 (nor_2_out, e0, e2);
  xor xor_2 (xor_2_out, e1, e3);
  and and_1 (s0, xor_1_out, nor_1_out);
  and and_2 (s1, nor_2_out, xor_2_out);

  // Notes on the sheet:
  //   2.8.a
endmodule
