// Logisim project 2.8.b.circ as structural Verilog: 1 circuit, main circuit main
module main (
  input  e3,
  input  e2,
  input  e1,
  input  e0,
  output v
);

  wire and_1_out, and_2_out, nand_1_out, nand_2_out, xor_1_out, xor_2_out;

  nand nand_1 (nand_1_out, e3, e2);
  xor xor_1 (xor_1_out, e1, e0);
  nand nand_2 (nand_2_out, e0, e1);
  xor xor_2 (xor_2_out, e2, e3);
  and and_1 (and_1_out, nand_1_out, xor_1_out);
  and and_2 (and_2_out, nand_2_out, xor_2_out);
  or or_1 (v, and_1_out, and_2_out);

  // Notes on the sheet:
  //   2.8.b
endmodule
